# Fritzing sketch Untitled Sketch (saved by Fritzing 0.9.3b)
breadboards: 1

parts:
  Part1 = Arduino Uno (Rev3)
  J1 = Basic Servo
  HC-SR04_Sensor_1 = HC-SR04 Ultrasonic Distance Sensor

nets:
  N1: Part1.D8, HC-SR04_Sensor_1.ECHO
  N2: Part1.D9_PWM, HC-SR04_Sensor_1.TRIG
  N3: Part1.D7, J1.pulse
  VCC: Part1.5V, J1.vcc, HC-SR04_Sensor_1.VCC
  GND: Part1.GND, J1.gnd, HC-SR04_Sensor_1.GND
